# Fritzing sketch Mincraft-ore-Cube (saved by Fritzing 1.0.4)
breadboards: 1

parts:
  Bauteil1 = Arduino Nano (Rev3.0)
  LED1 = RGB LED (com. cathode, rbg) [color="Red (633nm)" current=0.030A package="5 mm [THT]"]
  R1 = Resistor [tolerance=±5% power=0.25W resistance=220 package=THT]
  R2 = Resistor [tolerance=±5% power=0.25W resistance=220 package=THT]
  R3 = Resistor [tolerance=±5% power=0.25W resistance=220 package=THT]
  S1 = Pushbutton [package="[THT]"]

nets:
  N1: Bauteil1.D3, R1.Pin_1
  N2: Bauteil1.D4, LED1.blue_anode, S1.Pin_3, S1.Pin_4
  N3: Bauteil1.D5, R2.Pin_1
  N4: Bauteil1.D6, R3.Pin_1
  N5: Bauteil1.D12/MISO, S1.Pin_1, S1.Pin_2
  N6: LED1.red_anode, R3.Pin_0
  N7: LED1.common_cathode, R2.Pin_0
  N8: LED1.green_anode, R1.Pin_0
